// Logisim project Register_File.circ as structural Verilog: 1 circuit, main circuit main
module main (
  input  [4:0] rs,
  input  [31:0] write,
  input  [4:0] rt,
  input  [4:0] rd,
  output [31:0] crs,
  output [31:0] crt
);

  wire clock_1_out, undriven;
  wire [31:0] demultiplexer_1_out0, demultiplexer_1_out1, demultiplexer_1_out2, demultiplexer_1_out3,
       demultiplexer_1_out4, demultiplexer_1_out5, demultiplexer_1_out6, demultiplexer_1_out7,
       demultiplexer_1_out8, demultiplexer_1_out9, demultiplexer_1_out10, demultiplexer_1_out11,
       demultiplexer_1_out12, demultiplexer_1_out13, demultiplexer_1_out14, demultiplexer_1_out15,
       demultiplexer_1_out16, demultiplexer_1_out17, demultiplexer_1_out18, demultiplexer_1_out19,
       demultiplexer_1_out20, demultiplexer_1_out21, demultiplexer_1_out22, demultiplexer_1_out23,
       demultiplexer_1_out24, demultiplexer_1_out25, demultiplexer_1_out26, demultiplexer_1_out27,
       demultiplexer_1_out28, demultiplexer_1_out29, demultiplexer_1_out30, demultiplexer_1_out31,
       register_1_q, register_2_q, register_3_q, register_4_q, register_5_q, register_6_q, register_7_q,
       register_8_q, register_9_q, register_10_q, register_11_q, register_12_q, register_13_q, register_14_q,
       register_15_q, register_16_q, register_17_q, register_18_q, register_19_q, register_20_q,
       register_21_q, register_22_q, register_23_q, register_24_q, register_25_q, register_26_q,
       register_27_q, register_28_q, register_29_q, register_30_q, register_31_q, register_32_q, undriven_2;

  Demultiplexer #(.select(5), .width(32)) demultiplexer_1 (
    .out0(demultiplexer_1_out0), .out1(demultiplexer_1_out1), .out2(demultiplexer_1_out2),
    .out3(demultiplexer_1_out3), .out4(demultiplexer_1_out4), .out5(demultiplexer_1_out5),
    .out6(demultiplexer_1_out6), .out7(demultiplexer_1_out7), .out8(demultiplexer_1_out8),
    .out9(demultiplexer_1_out9), .out10(demultiplexer_1_out10), .out11(demultiplexer_1_out11),
    .out12(demultiplexer_1_out12), .out13(demultiplexer_1_out13), .out14(demultiplexer_1_out14),
    .out15(demultiplexer_1_out15), .out16(demultiplexer_1_out16), .out17(demultiplexer_1_out17),
    .out18(demultiplexer_1_out18), .out19(demultiplexer_1_out19), .out20(demultiplexer_1_out20),
    .out21(demultiplexer_1_out21), .out22(demultiplexer_1_out22), .out23(demultiplexer_1_out23),
    .out24(demultiplexer_1_out24), .out25(demultiplexer_1_out25), .out26(demultiplexer_1_out26),
    .out27(demultiplexer_1_out27), .out28(demultiplexer_1_out28), .out29(demultiplexer_1_out29),
    .out30(demultiplexer_1_out30), .out31(demultiplexer_1_out31), .in(write), .sel(rt));  // open: en
  Clock clock_1 (.out(clock_1_out));
  Register #(.width(32)) register_1 (
    .D(demultiplexer_1_out0), .en(undriven), .Q(register_1_q), .clk(clock_1_out));  // open: clr
  Register #(.width(32)) register_2 (.D(demultiplexer_1_out8), .Q(register_2_q), .clk(clock_1_out));  // open: en, clr
  Register #(.width(32)) register_3 (.D(demultiplexer_1_out16), .Q(register_3_q), .clk(clock_1_out));  // open: en, clr
  Register #(.width(32)) register_4 (.D(demultiplexer_1_out24), .Q(register_4_q), .clk(clock_1_out));  // open: en, clr
  Register #(.width(32)) register_5 (.D(demultiplexer_1_out1), .Q(register_5_q), .clk(clock_1_out));  // open: en, clr
  Register #(.width(32)) register_6 (.D(demultiplexer_1_out9), .Q(register_6_q), .clk(clock_1_out));  // open: en, clr
  Register #(.width(32)) register_7 (.D(demultiplexer_1_out17), .Q(register_7_q), .clk(clock_1_out));  // open: en, clr
  Register #(.width(32)) register_8 (.D(demultiplexer_1_out25), .Q(register_8_q), .clk(clock_1_out));  // open: en, clr
  Register #(.width(32)) register_9 (.D(demultiplexer_1_out2), .Q(register_9_q), .clk(clock_1_out));  // open: en, clr
  Register #(.width(32)) register_10 (
    .D(demultiplexer_1_out10), .Q(register_10_q), .clk(clock_1_out));  // open: en, clr
  Register #(.width(32)) register_11 (
    .D(demultiplexer_1_out18), .Q(register_11_q), .clk(clock_1_out));  // open: en, clr
  Register #(.width(32)) register_12 (
    .D(demultiplexer_1_out26), .Q(register_12_q), .clk(clock_1_out));  // open: en, clr
  Register #(.width(32)) register_13 (.D(demultiplexer_1_out3), .Q(register_13_q), .clk(clock_1_out));  // open: en, clr
  Register #(.width(32)) register_14 (
    .D(demultiplexer_1_out11), .Q(register_14_q), .clk(clock_1_out));  // open: en, clr
  Register #(.width(32)) register_15 (
    .D(demultiplexer_1_out19), .Q(register_15_q), .clk(clock_1_out));  // open: en, clr
  Register #(.width(32)) register_16 (
    .D(demultiplexer_1_out27), .Q(register_16_q), .clk(clock_1_out));  // open: en, clr
  Register #(.width(32)) register_17 (.D(demultiplexer_1_out4), .Q(register_17_q), .clk(clock_1_out));  // open: en, clr
  Register #(.width(32)) register_18 (
    .D(demultiplexer_1_out12), .Q(register_18_q), .clk(clock_1_out));  // open: en, clr
  Register #(.width(32)) register_19 (
    .D(demultiplexer_1_out20), .Q(register_19_q), .clk(clock_1_out));  // open: en, clr
  Register #(.width(32)) register_20 (
    .D(demultiplexer_1_out28), .Q(register_20_q), .clk(clock_1_out));  // open: en, clr
  Register #(.width(32)) register_21 (.D(demultiplexer_1_out5), .Q(register_21_q), .clk(clock_1_out));  // open: en, clr
  Register #(.width(32)) register_22 (
    .D(demultiplexer_1_out13), .Q(register_22_q), .clk(clock_1_out));  // open: en, clr
  Register #(.width(32)) register_23 (
    .D(demultiplexer_1_out21), .Q(register_23_q), .clk(clock_1_out));  // open: en, clr
  Register #(.width(32)) register_24 (
    .D(demultiplexer_1_out29), .Q(register_24_q), .clk(clock_1_out));  // open: en, clr
  Register #(.width(32)) register_25 (.D(demultiplexer_1_out6), .Q(register_25_q), .clk(clock_1_out));  // open: en, clr
  Register #(.width(32)) register_26 (
    .D(demultiplexer_1_out14), .Q(register_26_q), .clk(clock_1_out));  // open: en, clr
  Register #(.width(32)) register_27 (
    .D(demultiplexer_1_out22), .Q(register_27_q), .clk(clock_1_out));  // open: en, clr
  Register #(.width(32)) register_28 (
    .D(demultiplexer_1_out30), .Q(register_28_q), .clk(clock_1_out));  // open: en, clr
  Register #(.width(32)) register_29 (.D(demultiplexer_1_out7), .Q(register_29_q), .clk(clock_1_out));  // open: en, clr
  Register #(.width(32)) register_30 (
    .D(demultiplexer_1_out15), .Q(register_30_q), .clk(clock_1_out));  // open: en, clr
  Register #(.width(32)) register_31 (
    .D(demultiplexer_1_out23), .Q(register_31_q), .clk(clock_1_out));  // open: en, clr
  Register #(.width(32)) register_32 (
    .D(demultiplexer_1_out31), .Q(register_32_q), .clk(clock_1_out));  // open: en, clr
  Multiplexer #(.select(5), .width(32)) multiplexer_1 (
    .in0(register_29_q), .in1(register_25_q), .in2(register_21_q), .in3(register_17_q), .in4(register_13_q),
    .in5(register_9_q), .in6(register_5_q), .in7(register_1_q), .in8(register_30_q), .in9(register_26_q),
    .in10(register_22_q), .in11(register_18_q), .in12(register_14_q), .in13(register_10_q),
    .in14(register_6_q), .in15(register_2_q), .in16(register_31_q), .in17(register_27_q),
    .in18(register_23_q), .in19(register_19_q), .in20(register_15_q), .in21(register_11_q),
    .in22(register_7_q), .in23(register_3_q), .in24(register_32_q), .in25(register_28_q),
    .in26(register_24_q), .in27(register_20_q), .in28(register_16_q), .in29(register_12_q),
    .in30(register_8_q), .in31(register_4_q), .out(crs), .sel(rs));  // open: en
  Demultiplexer #(.select(5), .width(32)) demultiplexer_2 (
    .out0(register_29_q), .out1(register_25_q), .out2(register_21_q), .out3(register_17_q),
    .out4(register_13_q), .out5(register_9_q), .out6(register_5_q), .out7(register_1_q),
    .out8(register_30_q), .out9(register_26_q), .out10(register_22_q), .out11(register_18_q),
    .out12(register_14_q), .out13(register_10_q), .out14(register_6_q), .out15(register_2_q),
    .out16(register_31_q), .out17(register_27_q), .out18(register_23_q), .out19(register_19_q),
    .out20(register_15_q), .out21(register_11_q), .out22(register_7_q), .out23(register_3_q),
    .out24(register_32_q), .out25(register_28_q), .out26(register_24_q), .out27(register_20_q),
    .out28(register_16_q), .out29(register_12_q), .out30(register_8_q), .out31(register_4_q), .in(undriven_2));  // open: sel, en
endmodule
