// Logisim project ID-EX.circ as structural Verilog: 1 circuit, main circuit main
module main (
  input  [31:0] ID___RS,
  input  [31:0] ID___RT,
  input  [15:0] ID___Instruction__15_0,
  input  [4:0] ID___Instruction__20_16,
  input  [4:0] ID___Instruction__15_11,
  output [31:0] EX___RS,
  output [31:0] EX___RT,
  output [15:0] EX___Instruction__15_0,
  output [4:0] EX___Instruction__20_16,
  output [4:0] EX___Instruction__15_11
);

  Register #(.width(32)) Read_Data_1 (.D(ID___RS), .Q(EX___RS));  // open: en, clk, clr
  Register #(.width(32)) Read_Data_2 (.D(ID___RT), .Q(EX___RT));  // open: en, clk, clr
  Register #(.width(16)) Instruction__15_0 (
    .D(ID___Instruction__15_0), .Q(EX___Instruction__15_0));  // open: en, clk, clr
  Register #(.width(5)) Instruction__20_16 (
    .D(ID___Instruction__20_16), .Q(EX___Instruction__20_16));  // open: en, clk, clr
  Register #(.width(5)) Instruction__15_11 (
    .D(ID___Instruction__15_11), .Q(EX___Instruction__15_11));  // open: en, clk, clr
endmodule
