// Logisim project Entregable_2.circ as structural Verilog: 1 circuit, main circuit main
module main (
  input  [2:0] Index,
  input  [31:0] in_2,
  input  [10:0] in_3,
  input  Clock,
  output [31:0] out_5,
  output [10:0] out_6
);

  RAM #(.addrWidth(3), .dataWidth(11), .bus("separate")) ram_1 (
    .addr(Index), .din(in_3), .data(out_6), .clk(Clock));  // open: str, sel, ld, clr
  RAM #(.addrWidth(3), .dataWidth(32), .bus("separate")) ram_2 (
    .addr(Index), .din(in_2), .data(out_5), .clk(Clock));  // open: str, sel, ld, clr

  // Notes on the sheet:
  //   Tag
  //   Cache Block - Index / Tag
  //   Tag Output
  //   Cache Block
  //   Data-in
  //   Data
  //   Data-out
endmodule
