// Logisim project Entregable_3.circ as structural Verilog: 3 circuits, main circuit main
module main (
  input  [10:0] in_1,
  input  [2:0] in_2,
  input  [1:0] in_3,
  output [31:0] out_4,
  output out_5
);

  wire bitselector_1_out, clock_1_out, comparator_1_eq, comparator_2_eq, comparator_3_eq,
       selector_de_via_1_out_2, selector_de_via_1_out_3;
  wire [2:0] demultiplexer_1_out0, demultiplexer_1_out1, demultiplexer_3_out0, demultiplexer_3_out1,
       multiplexer_1_out, multiplexer_3_out;
  wire [10:0] cache_block_1_out_6, cache_block_2_out_6, demultiplexer_2_out0, demultiplexer_2_out1,
       demultiplexer_4_out0, demultiplexer_4_out1, multiplexer_2_out, multiplexer_4_out;
  wire [31:0] cache_block_1_out_5, cache_block_2_out_5, random_1_out;

  Selector_de_Via selector_de_via_1 (
    .in_1(clock_1_out), .out_2(selector_de_via_1_out_2), .out_3(selector_de_via_1_out_3));
  Clock clock_1 (.out(clock_1_out));
  Demultiplexer #(.width(3), .enable("false")) demultiplexer_1 (
    .out0(demultiplexer_1_out0), .out1(demultiplexer_1_out1), .in(in_2), .sel(selector_de_via_1_out_2));
  Demultiplexer #(.width(11), .enable("false")) demultiplexer_2 (
    .out0(demultiplexer_2_out0), .out1(demultiplexer_2_out1), .in(in_1), .sel(selector_de_via_1_out_2));
  Demultiplexer #(.width(3), .enable("false")) demultiplexer_3 (
    .out0(demultiplexer_3_out0), .out1(demultiplexer_3_out1), .in(in_2), .sel(selector_de_via_1_out_3));
  Demultiplexer #(.width(11), .enable("false")) demultiplexer_4 (
    .out0(demultiplexer_4_out0), .out1(demultiplexer_4_out1), .in(in_1), .sel(selector_de_via_1_out_3));
  Multiplexer #(.width(3), .enable("false")) multiplexer_1 (
    .in0(demultiplexer_1_out0), .in1(demultiplexer_1_out1), .out(multiplexer_1_out),
    .sel(selector_de_via_1_out_2));
  Multiplexer #(.width(11), .enable("false")) multiplexer_2 (
    .in0(demultiplexer_2_out0), .in1(demultiplexer_2_out1), .out(multiplexer_2_out),
    .sel(selector_de_via_1_out_2));
  Random #(.width(32)) random_1 (.clk(comparator_3_eq), .out(random_1_out));  // open: next, clr
  Multiplexer #(.width(3), .enable("false")) multiplexer_3 (
    .in0(demultiplexer_3_out0), .in1(demultiplexer_3_out1), .out(multiplexer_3_out),
    .sel(selector_de_via_1_out_3));
  Multiplexer #(.width(11), .enable("false")) multiplexer_4 (
    .in0(demultiplexer_4_out0), .in1(demultiplexer_4_out1), .out(multiplexer_4_out),
    .sel(selector_de_via_1_out_3));
  Cache_Block cache_block_1 (
    .Index(multiplexer_1_out), .in_3(multiplexer_2_out), .in_2(random_1_out),
    .Clock(selector_de_via_1_out_2), .out_6(cache_block_1_out_6), .out_5(cache_block_1_out_5));
  Cache_Block cache_block_2 (
    .Index(multiplexer_3_out), .in_3(multiplexer_4_out), .in_2(random_1_out),
    .Clock(selector_de_via_1_out_3), .out_6(cache_block_2_out_6), .out_5(cache_block_2_out_5));
  BitSelector #(.width(2)) bitselector_1 (.in(in_3), .out(bitselector_1_out), .sel(1'b1));
  Comparator #(.width(11)) comparator_1 (.a(in_1), .b(cache_block_1_out_6), .eq(comparator_1_eq));  // open: gt, lt
  Comparator #(.width(11)) comparator_2 (.a(cache_block_2_out_6), .b(in_1), .eq(comparator_2_eq));  // open: gt, lt
  Multiplexer #(.width(32), .enable("false")) multiplexer_5 (
    .in0(cache_block_1_out_5), .in1(cache_block_2_out_5), .out(out_4), .sel(bitselector_1_out));
  or Hit (out_5, comparator_1_eq, comparator_2_eq);
  Comparator #(.width(1)) comparator_3 (.a(out_5), .b(1'b0), .eq(comparator_3_eq));  // open: gt, lt

  // Notes on the sheet:
  //   16 bit Address
  //   Way Selector
  //   Index Plex
  //   Tag Plex
  //   Way 0
  //   Way 1
  //   Index Plex
  //   Tag Plex
  //   Way 0
  //   2-Way Associative Cache
  //   Emmanuel Zúñiga - B98729
  //   Way 1
  //   NOTA:
  //   Cualquier tag conformado por 0's en cualquier indice puede dar un hit
  //   Ya que la RAM asume que es el mismo dato
  //   Si se quiere introducir una dirección de 16 bits hay que hacerlo en diferentes ciclos para obtener resultados
  //   Dado que las Memorias RAM de Logisim tienen como valor por defecto el 0
  //   Data
  //   Si es un Miss
  //   Hit = 1
  //   Miss = 0
  //   La cache hace la lectura y escritura en un único ciclo del reloj, por lo tanto
endmodule

module Selector_de_Via (
  input  in_1,
  output out_2,
  output out_3
);

  wire random_1_out;

  Random #(.width(1)) random_1 (.clk(in_1), .out(random_1_out));  // open: next, clr
  Demultiplexer demultiplexer_1 (.out0(out_2), .out1(out_3), .in(random_1_out), .sel(in_1));  // open: en
endmodule

module Cache_Block (
  input  [2:0] Index,
  input  [31:0] in_2,
  input  [10:0] in_3,
  input  Clock,
  output [31:0] out_5,
  output [10:0] out_6
);

  RAM #(.addrWidth(3), .dataWidth(11), .bus("separate")) ram_1 (
    .addr(Index), .din(in_3), .data(out_6), .clk(Clock));  // open: str, sel, ld, clr
  RAM #(.addrWidth(3), .dataWidth(32), .bus("separate")) ram_2 (
    .addr(Index), .din(in_2), .data(out_5), .clk(Clock));  // open: str, sel, ld, clr

  // Notes on the sheet:
  //   Tag
  //   Cache Block - Index / Tag
  //   Tag Output
  //   Data-in
  //   Data
  //   Data-out
endmodule
