// Logisim project B98729 - CPU_Main.circ as structural Verilog: 16 circuits, main circuit main
module main (
  input  Enable,
  input  Clear
);

  wire alu_1_zero_flag, Branch_out, Clock_out, Control_Unit_jump, ex_mem_1_mem___zero_flag;
  wire [1:0] Control_Unit_access_type, Control_Unit_wb, ex_mem_1_mem___access_type,
       ex_mem_1_mem___wb_signals, id_ex_1_ex___access_type, id_ex_1_ex___wb_signal, mem_wb_1_wb___wb_signals;
  wire [2:0] Control_Unit_mem, ex_mem_1_mem___mem_signals, id_ex_1_ex___mem_signal;
  wire [3:0] id_ex_1_ex___ex_signal_2;
  wire [4:0] ex_mem_1_mem___rd, id_ex_1_ex___instruction__15_11, id_ex_1_ex___instruction__20_16,
       mem_wb_1_wb_write_register, multiplexer_2_out;
  wire [5:0] Control_Unit_ex, id_ex_1_ex___ex_signal, if_id_1_id___instruction_2;
  wire [25:0] if_id_1_id___instruction;
  wire [27:0] bit_extender_1_out;
  wire [31:0] adder_1_out, adder_2_out, alu_1_y, bit_extender_2_out, data_memory_1_dataout,
       ex_mem_1_mem___alu_result, ex_mem_1_mem___rs_data, id_ex_1_ex____pc___4, id_ex_1_ex___immediate,
       id_ex_1_ex___rs, id_ex_1_ex___rt, if_id_1_id___pc___4, mem_wb_1_wb___read_data,
       mem_wb_1_wb___write_data, multiplexer_1_out, multiplexer_3_out, pc_mux_1_pc_mux, PC_q,
       register_file_1_crs, register_file_1_crt, rom_1_data, shifter_1_out;

  // Probe on pc_mux_1_pc_mux
  // Probe on PC_q
  Register #(.width(32), .Select("low")) PC (.D(pc_mux_1_pc_mux), .Q(PC_q), .clk(Clock_out), .clr(Clear));  // open: en
  // Probe on PC_q[11:2]
  PC_Mux pc_mux_1 (
    .PC_4(adder_1_out), .MEM_PC(adder_2_out), .JUMP_2({PC_q[31:28], bit_extender_1_out}),
    .Branch(Branch_out), .Jump(Control_Unit_jump), .PC_MUX(pc_mux_1_pc_mux));
  Adder_part #(.width(32)) adder_1 (.a(PC_q), .b(32'h4), .out(adder_1_out));  // open: cin, cout
  ROM #(.addrWidth(10), .dataWidth(32), .Select("high")) rom_1 (.addr(PC_q[11:2]), .data(rom_1_data));
  IF_ID if_id_1 (
    .IF___PC___4(adder_1_out), .IF___Instruction(rom_1_data), .Clock(Clock_out), .Clear(Clear),
    .Enable(Enable), .ID___Instruction({if_id_1_id___instruction_2, if_id_1_id___instruction}),
    .ID___PC___4(if_id_1_id___pc___4));
  Clock Clock (.out(Clock_out));
  // Probe on if_id_1_id___instruction[25:21]
  // Probe on if_id_1_id___instruction[20:16]
  // Probe on mem_wb_1_wb_write_register
  Control_Unit Control_Unit (
    .Opcode(if_id_1_id___instruction_2), .Function(if_id_1_id___instruction[5:0]), .WB(Control_Unit_wb),
    .MEM(Control_Unit_mem), .EX(Control_Unit_ex), .JUMP(Control_Unit_jump),
    .Access_Type(Control_Unit_access_type));
  assign bit_extender_1_out = {{2{1'b0}}, if_id_1_id___instruction};  // Bit_Extender bit_extender_1
  assign bit_extender_2_out = {{16{1'b0}}, if_id_1_id___instruction[15:0]};  // Bit_Extender bit_extender_2
  // Probe on mem_wb_1_wb___wb_signals[1]
  // Probe on register_file_1_crs
  // Probe on register_file_1_crt
  Register_File register_file_1 (
    .Clock(Clock_out), .RegWrite(mem_wb_1_wb___wb_signals[1]), .RS(if_id_1_id___instruction[25:21]),
    .Write_Data(multiplexer_3_out), .RT(if_id_1_id___instruction[20:16]), .RD(mem_wb_1_wb_write_register),
    .CRS(register_file_1_crs), .CRT(register_file_1_crt));
  // Probe on if_id_1_id___instruction[20:16]
  // Probe on if_id_1_id___instruction[15:11]
  ID_EX id_ex_1 (
    .Clock(Clock_out), .Clear(Clear), .Enable(Enable), .WB_Signal(Control_Unit_wb),
    .Mem_Signal(Control_Unit_mem), .EX_Signal(Control_Unit_ex), .ID____PC___4(if_id_1_id___pc___4),
    .ID___RS(register_file_1_crs), .ID___RT(register_file_1_crt), .ID___Immediate(bit_extender_2_out),
    .ID___Instruction__20_16(if_id_1_id___instruction[20:16]),
    .ID___Instruction__15_11(if_id_1_id___instruction[15:11]), .EX___WB_Signal(id_ex_1_ex___wb_signal),
    .EX___Mem_Signal(id_ex_1_ex___mem_signal),
    .EX___Ex_Signal({id_ex_1_ex___ex_signal[5], id_ex_1_ex___ex_signal_2, id_ex_1_ex___ex_signal[0]}),
    .EX____PC___4(id_ex_1_ex____pc___4), .EX___RS(id_ex_1_ex___rs), .EX___RT(id_ex_1_ex___rt),
    .EX___Immediate(id_ex_1_ex___immediate), .EX___Instruction__20_16(id_ex_1_ex___instruction__20_16),
    .EX___Instruction__15_11(id_ex_1_ex___instruction__15_11), .ID___Access_Type(Control_Unit_access_type),
    .EX___Access_Type(id_ex_1_ex___access_type));
  Multiplexer #(.width(32), .enable("false")) multiplexer_1 (
    .in0(id_ex_1_ex___rt), .in1(id_ex_1_ex___immediate), .out(multiplexer_1_out),
    .sel(id_ex_1_ex___ex_signal[0]));
  Shifter #(.width(32)) shifter_1 (.in(id_ex_1_ex___immediate), .\dist (5'b00010), .out(shifter_1_out));
  ALU alu_1 (
    .A(id_ex_1_ex___rs), .Y(alu_1_y), .B(multiplexer_1_out), .Zero_Flag(alu_1_zero_flag),
    .Opcode(id_ex_1_ex___ex_signal_2));  // open: Cin, Cout
  // Probe on id_ex_1_ex___rt
  // Probe on multiplexer_2_out
  Multiplexer #(.width(5), .enable("false")) multiplexer_2 (
    .in0(id_ex_1_ex___instruction__20_16), .in1(id_ex_1_ex___instruction__15_11), .out(multiplexer_2_out),
    .sel(id_ex_1_ex___ex_signal[5]));
  Adder_part #(.width(32)) adder_2 (.a(id_ex_1_ex____pc___4), .b(shifter_1_out), .out(adder_2_out));  // open: cin, cout
  // Probe on alu_1_y
  EX_MEM ex_mem_1 (
    .Clock(Clock_out), .Clear(Clear), .Enable(Enable), .EX___WB_Signals(id_ex_1_ex___wb_signal),
    .EX___MEM_Signals(id_ex_1_ex___mem_signal), .EX___Zero_Flag(alu_1_zero_flag), .EX___ALU_Result(alu_1_y),
    .EX___RS_Data(id_ex_1_ex___rt), .EX___RD(multiplexer_2_out),
    .MEM___WB_Signals(ex_mem_1_mem___wb_signals), .MEM___MEM_Signals(ex_mem_1_mem___mem_signals),
    .MEM___Zero_Flag(ex_mem_1_mem___zero_flag), .MEM___ALU_Result(ex_mem_1_mem___alu_result),
    .MEM___RS_Data(ex_mem_1_mem___rs_data), .MEM___RD(ex_mem_1_mem___rd),
    .EX___Access_Type(id_ex_1_ex___access_type), .MEM___Access_Type(ex_mem_1_mem___access_type));
  // Probe on ex_mem_1_mem___rs_data
  // Probe on ex_mem_1_mem___alu_result[11:0]
  // Probe on ex_mem_1_mem___rd
  and Branch (Branch_out, ex_mem_1_mem___mem_signals[2], ex_mem_1_mem___zero_flag);
  // Probe on ex_mem_1_mem___mem_signals
  Data_Memory data_memory_1 (
    .Address(ex_mem_1_mem___alu_result[11:0]), .DataIn(ex_mem_1_mem___rs_data),
    .MemRead(ex_mem_1_mem___mem_signals[1]), .MemWrite(ex_mem_1_mem___mem_signals[0]), .Clock(Clock_out),
    .Access_Type(ex_mem_1_mem___access_type), .DataOut(data_memory_1_dataout));
  // Probe on data_memory_1_dataout
  // Probe on ex_mem_1_mem___alu_result
  MEM_WB mem_wb_1 (
    .MEM___WB_Signals(ex_mem_1_mem___wb_signals), .MEM___Read_Data(data_memory_1_dataout),
    .MEM___Write_Data(ex_mem_1_mem___alu_result), .Mem_Write_Register(ex_mem_1_mem___rd),
    .WB___WB_Signals(mem_wb_1_wb___wb_signals), .WB___Read_Data(mem_wb_1_wb___read_data),
    .WB___Write_Data(mem_wb_1_wb___write_data), .WB_Write_Register(mem_wb_1_wb_write_register),
    .Clock(Clock_out), .Clear(Clear), .Enable(Enable));  // open: MEM___Access_Type, WB___Access_Type
  Multiplexer #(.width(32), .enable("false")) multiplexer_3 (
    .in0(mem_wb_1_wb___write_data), .in1(mem_wb_1_wb___read_data), .out(multiplexer_3_out),
    .sel(mem_wb_1_wb___wb_signals[0]));
  // Probe on multiplexer_3_out

  // Notes on the sheet:
  //   B98729 - CPU
  //   Conecta con EX/MEM
  //   IF
  //   Instruction Memory
  //   JUMP
  //   Branch
  //   PC + 4
  //   contents of rom_1 (hex, n*v repeats v):
  //   ac010020 84020020 a1410064 8d430064
  //   isJump
  //   Operation
  //   Function
  //   JUMP
  //   PC
  //   WriteRegister
  //   WriteData
  //   ID
  //   WB
  //   Mem
  //   EX
  //   Clock
  //   Immediate
  //   RS Data
  //   RT Data
  //   Conecta con MEM/WB
  //   Enable
  //   Clear
  //   Clock
  //   WB
  //   EX
  //   AluSrc
  //   RD
  //   RegDst
  //   Opcode
  //   Enable
  //   RD
  //   Clock
  //   WB
  //   Mem
  //   Clear
  //   ALU Result
  //   PCSrc
  //   Memread
  //   MemWrite
  //   Enable
  //   ReadData
  //   Clock
  //   WB
  //   Clear
  //   RegWrite
  //   MemToReg
  //   Write Register
  //   Write Data
endmodule

module IF_ID (
  input  Clock,
  input  Clear,
  input  Enable,
  input  [31:0] IF___PC___4,
  input  [31:0] IF___Instruction,
  output [31:0] ID___PC___4,
  output [31:0] ID___Instruction
);

  Register #(.width(32), .Select("low")) PC_4 (.D(IF___PC___4), .en(Enable), .Q(ID___PC___4), .clk(Clock), .clr(Clear));
  Register #(.width(32), .Select("low")) Instruction (
    .D(IF___Instruction), .en(Enable), .Q(ID___Instruction), .clk(Clock), .clr(Clear));

  // Notes on the sheet:
  //   B98729 - IF/ID
  //   Inputs
  //   Outputs
endmodule

module ID_EX (
  input  Clock,
  input  Clear,
  input  Enable,
  input  [1:0] WB_Signal,
  input  [2:0] Mem_Signal,
  input  [5:0] EX_Signal,
  input  [31:0] ID____PC___4,
  input  [31:0] ID___RS,
  input  [31:0] ID___RT,
  input  [31:0] ID___Immediate,
  input  [4:0] ID___Instruction__20_16,
  input  [4:0] ID___Instruction__15_11,
  input  [1:0] ID___Access_Type,
  output [1:0] EX___WB_Signal,
  output [2:0] EX___Mem_Signal,
  output [5:0] EX___Ex_Signal,
  output [31:0] EX____PC___4,
  output [31:0] EX___RS,
  output [31:0] EX___RT,
  output [31:0] EX___Immediate,
  output [4:0] EX___Instruction__20_16,
  output [4:0] EX___Instruction__15_11,
  output [1:0] EX___Access_Type
);

  Register #(.width(2), .Select("low")) register_1 (
    .D(WB_Signal), .en(Enable), .Q(EX___WB_Signal), .clk(Clock), .clr(Clear));
  Register #(.width(3), .Select("low")) register_2 (
    .D(Mem_Signal), .en(Enable), .Q(EX___Mem_Signal), .clk(Clock), .clr(Clear));
  Register #(.width(6), .Select("low")) register_3 (
    .D(EX_Signal), .en(Enable), .Q(EX___Ex_Signal), .clk(Clock), .clr(Clear));
  Register #(.width(2), .Select("low")) register_4 (
    .D(ID___Access_Type), .en(Enable), .Q(EX___Access_Type), .clk(Clock), .clr(Clear));
  Register #(.width(32), .Select("low")) PC___4 (
    .D(ID____PC___4), .en(Enable), .Q(EX____PC___4), .clk(Clock), .clr(Clear));
  Register #(.width(32), .Select("low")) Read_Data_1 (.D(ID___RS), .en(Enable), .Q(EX___RS), .clk(Clock), .clr(Clear));
  Register #(.width(32), .Select("low")) Read_Data_2 (.D(ID___RT), .en(Enable), .Q(EX___RT), .clk(Clock), .clr(Clear));
  Register #(.width(32), .Select("low")) Immediate (
    .D(ID___Immediate), .en(Enable), .Q(EX___Immediate), .clk(Clock), .clr(Clear));
  Register #(.width(5), .Select("low")) Instruction__20_16 (
    .D(ID___Instruction__20_16), .en(Enable), .Q(EX___Instruction__20_16), .clk(Clock), .clr(Clear));
  Register #(.width(5), .Select("low")) Instruction__15_11 (
    .D(ID___Instruction__15_11), .en(Enable), .Q(EX___Instruction__15_11), .clk(Clock), .clr(Clear));

  // Notes on the sheet:
  //   B98729 - ID/EX
  //   Inputs
  //   Outputs
endmodule

module Register_File (
  input  Clock,
  input  RegWrite,
  input  [4:0] RS,
  input  [31:0] Write_Data,
  input  [4:0] RT,
  input  [4:0] RD,
  output [31:0] CRS,
  output [31:0] CRT
);

  wire _0, _1, _2, _3, _4, _5, _6, _7, _8, _9, _10, _11, _12, _13, _14, _15, _16, _17, _18, _19, _20, _21,
       _22, _23, _24, _25, _26, _27, _28, _29, _30, _31;
  wire [31:0] R0, R0_t, R1, R2, R3, R4, R5, R6, R7, R7_t, R8, R9, R9_t, R10, R11, R12, R13, R14, R15, R16,
       R17, R18, R19, R20, R21, R22, R23, R24, R25, R26, R27, R28, R29, R30, R31;

  Decoder #(.select(5), .disabled(0)) decoder_1 (
    .out1(_1), .out2(_2), .out3(_3), .out4(_4), .out5(_5), .out6(_6), .out7(_7), .out8(_8), .out9(_9),
    .out10(_10), .out11(_11), .out12(_12), .out13(_13), .out14(_14), .out15(_15), .out16(_16), .out17(_17),
    .out18(_18), .out19(_19), .out20(_20), .out21(_21), .out22(_22), .out23(_23), .out24(_24), .out25(_25),
    .out26(_26), .out27(_27), .out28(_28), .out29(_29), .out30(_30), .out31(_31), .sel(RD), .en(RegWrite));  // open: out0
  Register #(.width(32), .trigger("falling"), .Select("low")) register_1 (
    .D({32{1'b0}}), .en(_0), .Q(R0_t));  // open: clk, clr
  Register #(.width(32), .trigger("falling"), .Select("low")) register_2 (
    .D(Write_Data), .en(_4), .Q(R4), .clk(Clock));  // open: clr
  Register #(.width(32), .trigger("falling"), .Select("low")) register_3 (
    .D(Write_Data), .en(_8), .Q(R8), .clk(Clock));  // open: clr
  Register #(.width(32), .trigger("falling"), .Select("low")) register_4 (
    .D(Write_Data), .en(_12), .Q(R12), .clk(Clock));  // open: clr
  Register #(.width(32), .trigger("falling"), .Select("low")) register_5 (
    .D(Write_Data), .en(_16), .Q(R16), .clk(Clock));  // open: clr
  Register #(.width(32), .trigger("falling"), .Select("low")) register_6 (
    .D(Write_Data), .en(_20), .Q(R20), .clk(Clock));  // open: clr
  Register #(.width(32), .trigger("falling"), .Select("low")) register_7 (
    .D(Write_Data), .en(_24), .Q(R24), .clk(Clock));  // open: clr
  Register #(.width(32), .trigger("falling"), .Select("low")) register_8 (
    .D(Write_Data), .en(_28), .Q(R28), .clk(Clock));  // open: clr
  Register #(.width(32), .trigger("falling"), .Select("low")) register_9 (
    .D(Write_Data), .en(_1), .Q(R1), .clk(Clock));  // open: clr
  Register #(.width(32), .trigger("falling"), .Select("low")) register_10 (
    .D(Write_Data), .en(_5), .Q(R5), .clk(Clock));  // open: clr
  Register #(.width(32), .trigger("falling"), .Select("low")) register_11 (
    .D(Write_Data), .en(_9), .Q(R9_t), .clk(Clock));  // open: clr
  Register #(.width(32), .trigger("falling"), .Select("low")) register_12 (
    .D(Write_Data), .en(_13), .Q(R13), .clk(Clock));  // open: clr
  Register #(.width(32), .trigger("falling"), .Select("low")) register_13 (
    .D(Write_Data), .en(_17), .Q(R17), .clk(Clock));  // open: clr
  Register #(.width(32), .trigger("falling"), .Select("low")) register_14 (
    .D(Write_Data), .en(_21), .Q(R21), .clk(Clock));  // open: clr
  Register #(.width(32), .trigger("falling"), .Select("low")) register_15 (
    .D(Write_Data), .en(_25), .Q(R25), .clk(Clock));  // open: clr
  Register #(.width(32), .trigger("falling"), .Select("low")) register_16 (
    .D(Write_Data), .en(_29), .Q(R29), .clk(Clock));  // open: clr
  Register #(.width(32), .trigger("falling"), .Select("low")) register_17 (
    .D(Write_Data), .en(_2), .Q(R2), .clk(Clock));  // open: clr
  Register #(.width(32), .trigger("falling"), .Select("low")) register_18 (
    .D(Write_Data), .en(_6), .Q(R6), .clk(Clock));  // open: clr
  Register #(.width(32), .trigger("falling"), .Select("low")) register_19 (
    .D(Write_Data), .en(_10), .Q(R10), .clk(Clock));  // open: clr
  Register #(.width(32), .trigger("falling"), .Select("low")) register_20 (
    .D(Write_Data), .en(_14), .Q(R14), .clk(Clock));  // open: clr
  Register #(.width(32), .trigger("falling"), .Select("low")) register_21 (
    .D(Write_Data), .en(_18), .Q(R18), .clk(Clock));  // open: clr
  Register #(.width(32), .trigger("falling"), .Select("low")) register_22 (
    .D(Write_Data), .en(_22), .Q(R22), .clk(Clock));  // open: clr
  Register #(.width(32), .trigger("falling"), .Select("low")) register_23 (
    .D(Write_Data), .en(_26), .Q(R26), .clk(Clock));  // open: clr
  Register #(.width(32), .trigger("falling"), .Select("low")) register_24 (
    .D(Write_Data), .en(_30), .Q(R30), .clk(Clock));  // open: clr
  Register #(.width(32), .trigger("falling"), .Select("low")) register_25 (
    .D(Write_Data), .en(_3), .Q(R3), .clk(Clock));  // open: clr
  Register #(.width(32), .trigger("falling"), .Select("low")) register_26 (
    .D(Write_Data), .en(_7), .Q(R7_t), .clk(Clock));  // open: clr
  Register #(.width(32), .trigger("falling"), .Select("low")) register_27 (
    .D(Write_Data), .en(_11), .Q(R11), .clk(Clock));  // open: clr
  Register #(.width(32), .trigger("falling"), .Select("low")) register_28 (
    .D(Write_Data), .en(_15), .Q(R15), .clk(Clock));  // open: clr
  Register #(.width(32), .trigger("falling"), .Select("low")) register_29 (
    .D(Write_Data), .en(_19), .Q(R19), .clk(Clock));  // open: clr
  Register #(.width(32), .trigger("falling"), .Select("low")) register_30 (
    .D(Write_Data), .en(_23), .Q(R23), .clk(Clock));  // open: clr
  Register #(.width(32), .trigger("falling"), .Select("low")) register_31 (
    .D(Write_Data), .en(_27), .Q(R27), .clk(Clock));  // open: clr
  Register #(.width(32), .trigger("falling"), .Select("low")) register_32 (
    .D(Write_Data), .en(_31), .Q(R31), .clk(Clock));  // open: clr
  Multiplexer #(.select(5), .width(32), .disabled(0), .enable("false")) multiplexer_1 (
    .in0(R0), .in1(R1), .in2(R2), .in3(R3), .in4(R4), .in5(R5), .in6(R6), .in7(R7), .in8(R8), .in9(R9),
    .in10(R10), .in11(R11), .in12(R12), .in13(R13), .in14(R14), .in15(R15), .in16(R16), .in17(R17),
    .in18(R18), .in19(R19), .in20(R20), .in21(R21), .in22(R22), .in23(R23), .in24(R24), .in25(R25),
    .in26(R26), .in27(R27), .in28(R28), .in29(R29), .in30(R30), .in31(R31), .out(CRS), .sel(RS));
  Multiplexer #(.select(5), .width(32), .disabled(0), .enable("false")) multiplexer_2 (
    .in0(R0), .in1(R1), .in2(R2), .in3(R3), .in4(R4), .in5(R5), .in6(R6), .in7(R7), .in8(R8), .in9(R9),
    .in10(R10), .in11(R11), .in12(R12), .in13(R13), .in14(R14), .in15(R15), .in16(R16), .in17(R17),
    .in18(R18), .in19(R19), .in20(R20), .in21(R21), .in22(R22), .in23(R23), .in24(R24), .in25(R25),
    .in26(R26), .in27(R27), .in28(R28), .in29(R29), .in30(R30), .in31(R31), .out(CRT), .sel(RT));

  // Notes on the sheet:
  //   B98279 - Register File
  //   Inputs
  //   Outputs
endmodule

module Control_Unit (
  input  [5:0] Opcode,
  input  [5:0] Function,
  output [1:0] WB,
  output [2:0] MEM,
  output [5:0] EX,
  output JUMP,
  output [1:0] Access_Type
);

  wire and_1_out, and_2_out, comparator_1_eq, comparator_2_eq, comparator_3_eq, comparator_4_eq,
       comparator_5_eq, comparator_7_eq, comparator_8_eq, IsSyscall;
  wire [10:0] rom_1_data, rom_2_data;

  // Probe on Opcode
  // Probe on Function
  // Probe on Opcode
  ROM #(.addrWidth(6), .dataWidth(11), .Select("high")) rom_1 (.addr(Opcode), .data(rom_1_data));
  ROM #(.addrWidth(6), .dataWidth(11), .Select("high")) rom_2 (.addr(Function), .data(rom_2_data));
  Comparator #(.width(6), .mode("unsigned")) comparator_1 (
    .a(Opcode), .b({6{1'b0}}), .eq(comparator_1_eq));  // open: gt, lt
  Comparator #(.width(6), .mode("unsigned")) comparator_2 (
    .a(Function), .b(6'b001000), .eq(comparator_2_eq));  // open: gt, lt
  Comparator #(.width(6), .mode("unsigned")) comparator_3 (
    .a(Function), .b(6'b001001), .eq(comparator_3_eq));  // open: gt, lt
  Comparator #(.width(6), .mode("unsigned")) comparator_4 (
    .a(Opcode), .b(6'b000010), .eq(comparator_4_eq));  // open: gt, lt
  Comparator #(.width(6), .mode("unsigned")) comparator_5 (
    .a(Opcode), .b(6'b000011), .eq(comparator_5_eq));  // open: gt, lt
  Comparator #(.width(6), .mode("unsigned")) comparator_6 (
    .a(Function), .b(6'b001100), .eq(IsSyscall));  // open: gt, lt
  ROM #(.addrWidth(6), .dataWidth(2), .Select("high")) rom_3 (.addr(Opcode), .data(Access_Type));
  Comparator #(.width(6), .mode("unsigned")) comparator_7 (
    .a(Opcode), .b({6{1'b0}}), .eq(comparator_7_eq));  // open: gt, lt
  Comparator #(.width(6), .mode("unsigned")) comparator_8 (
    .a(Opcode), .b({6{1'b0}}), .eq(comparator_8_eq));  // open: gt, lt
  and and_1 (and_1_out, comparator_2_eq, comparator_7_eq);
  and and_2 (and_2_out, comparator_3_eq, comparator_8_eq);
  Multiplexer #(.width(2), .enable("false")) multiplexer_1 (
    .in0(rom_1_data[10:9]), .in1(rom_2_data[10:9]), .out(WB), .sel(comparator_1_eq));
  Multiplexer #(.width(3), .enable("false")) multiplexer_2 (
    .in0(rom_1_data[8:6]), .in1(rom_2_data[8:6]), .out(MEM), .sel(comparator_1_eq));
  Multiplexer #(.enable("false")) multiplexer_3 (
    .in0(rom_1_data[5]), .in1(rom_2_data[5]), .out(EX[5]), .sel(comparator_1_eq));
  Multiplexer #(.width(4), .enable("false")) multiplexer_4 (
    .in0(rom_1_data[4:1]), .in1(rom_2_data[4:1]), .out(EX[4:1]), .sel(comparator_1_eq));
  Multiplexer #(.enable("false")) multiplexer_5 (
    .in0(rom_1_data[0]), .in1(rom_2_data[0]), .out(EX[0]), .sel(comparator_1_eq));
  or or_1 (JUMP, and_1_out, and_2_out, comparator_4_eq, comparator_5_eq);

  // Notes on the sheet:
  //   La utilización de constantes
  //   permite la simplificación del circuito
  //   B98729 - Control Unit
  //   De momento solo se encuentran codificadas ciertas instrucciones
  //   Function
  //   OpCode
  //   contents of rom_1 (hex, n*v repeats v):
  //   0 0 20 20 119 119 11f 11f 401 401 411 411 403 405 407 17*0 6*681 0 0 7*61 0 6a1 0 0 0 6a1 0 0 6a1
  //   6a1 0 0 0 6a1 0 0 6a1
  //   contents of rom_2 (hex, n*v repeats v):
  //   42c 0 428 21*0 216 0 216 5*0 420 420 438 438 422 424 426 0 0 0 430 430
  //   Function
  //   contents of rom_3 (hex, n*v repeats v):
  //   33*0 1 2 0 0 1 0 0 0 1 2 2 0 0 2
  //   Opcode
  //   Function
  //   Señales
  //   Señal que determina si la instrucción es un salto
  //   EX
  //   Inputs
  //   Outputs
endmodule

module EX_MEM (
  input  Clock,
  input  Clear,
  input  Enable,
  input  [1:0] EX___WB_Signals,
  input  [2:0] EX___MEM_Signals,
  input  EX___Zero_Flag,
  input  [31:0] EX___ALU_Result,
  input  [31:0] EX___RS_Data,
  input  [4:0] EX___RD,
  input  [1:0] EX___Access_Type,
  output [1:0] MEM___WB_Signals,
  output [2:0] MEM___MEM_Signals,
  output MEM___Zero_Flag,
  output [31:0] MEM___ALU_Result,
  output [31:0] MEM___RS_Data,
  output [4:0] MEM___RD,
  output [1:0] MEM___Access_Type
);

  Register #(.width(2), .Select("low")) WB_Signals (
    .D(EX___WB_Signals), .en(Enable), .Q(MEM___WB_Signals), .clk(Clock), .clr(Clear));
  Register #(.width(3), .Select("low")) MEM_Signals (
    .D(EX___MEM_Signals), .en(Enable), .Q(MEM___MEM_Signals), .clk(Clock), .clr(Clear));
  Register #(.width(2), .Select("low")) Access_Type (
    .D(EX___Access_Type), .en(Enable), .Q(MEM___Access_Type), .clk(Clock), .clr(Clear));
  Register #(.width(1), .Select("low")) Zero_Flag (
    .D(EX___Zero_Flag), .en(Enable), .Q(MEM___Zero_Flag), .clk(Clock), .clr(Clear));
  Register #(.width(32), .Select("low")) ALU_Result (
    .D(EX___ALU_Result), .en(Enable), .Q(MEM___ALU_Result), .clk(Clock), .clr(Clear));
  Register #(.width(32), .Select("low")) RS_Data (
    .D(EX___RS_Data), .en(Enable), .Q(MEM___RS_Data), .clk(Clock), .clr(Clear));
  Register #(.width(5), .Select("low")) RD (.D(EX___RD), .en(Enable), .Q(MEM___RD), .clk(Clock), .clr(Clear));

  // Notes on the sheet:
  //   B98729 - EX/MEM
  //   Inputs
  //   Outputs
endmodule

module MEM_WB (
  input  Clock,
  input  Clear,
  input  Enable,
  input  [1:0] MEM___WB_Signals,
  input  [31:0] MEM___Read_Data,
  input  [31:0] MEM___Write_Data,
  input  [4:0] Mem_Write_Register,
  input  [1:0] MEM___Access_Type,
  output [1:0] WB___WB_Signals,
  output [31:0] WB___Read_Data,
  output [31:0] WB___Write_Data,
  output [4:0] WB_Write_Register,
  output [1:0] WB___Access_Type
);

  Register #(.width(2), .Select("low")) WB_Signals (
    .D(MEM___WB_Signals), .en(Enable), .Q(WB___WB_Signals), .clk(Clock), .clr(Clear));
  Register #(.width(2), .Select("low")) Access_Type (
    .D(MEM___Access_Type), .en(Enable), .Q(WB___Access_Type), .clk(Clock), .clr(Clear));
  Register #(.width(32), .Select("low")) Read_Data (
    .D(MEM___Read_Data), .en(Enable), .Q(WB___Read_Data), .clk(Clock), .clr(Clear));
  Register #(.width(32), .Select("low")) Write_Data (
    .D(MEM___Write_Data), .en(Enable), .Q(WB___Write_Data), .clk(Clock), .clr(Clear));
  Register #(.width(5), .Select("low")) Write_Register (
    .D(Mem_Write_Register), .en(Enable), .Q(WB_Write_Register), .clk(Clock), .clr(Clear));

  // Notes on the sheet:
  //   B98729 - MEM/WB
  //   Inputs
  //   Outputs
endmodule

module Adder (
  input  Cin,
  input  [31:0] A,
  input  [31:0] B,
  output [31:0] Result,
  output Overflow
);

  wire adder_1_cout, adder_2_cout;

  Adder_part #(.width(31)) adder_1 (.a(A[30:0]), .b(B[30:0]), .out(Result[30:0]), .cin(Cin), .cout(adder_1_cout));
  Adder_part #(.width(1)) adder_2 (.a(A[31]), .b(B[31]), .out(Result[31]), .cin(adder_1_cout), .cout(adder_2_cout));
  xor xor_1 (Overflow, adder_1_cout, adder_2_cout);

  // Notes on the sheet:
  //   ALU - B98729
  //   Inputs
  //   Outputs
endmodule

module Sub (
  input  Cin,
  input  [31:0] A,
  input  [31:0] B,
  output [31:0] Result,
  output Carry_Flag
);

  wire adder_1_cout, adder_2_cout, adder_2_out;
  wire [30:0] negator_1_out;

  Negator #(.width(31)) negator_1 (.in(B[30:0]), .out(negator_1_out));
  Adder_part #(.width(31)) adder_1 (.a(A[30:0]), .b(negator_1_out), .out(Result[30:0]), .cin(Cin), .cout(adder_1_cout));
  Adder_part #(.width(1)) adder_2 (.a(A[31]), .b(B[31]), .out(adder_2_out), .cin(adder_1_cout), .cout(adder_2_cout));
  xor xor_1 (Carry_Flag, adder_1_cout, adder_2_cout);
  not not_1 (Result[31], adder_2_out);

  // Notes on the sheet:
  //   ALU - B98729
  //   Inputs
  //   Outputs
endmodule

module Multiplier (
  input  Cin,
  input  [31:0] A,
  input  [31:0] B,
  output [31:0] Result,
  output Carry_Flag
);

  wire [31:0] bit_extender_1_out, multiplier_1_cout;

  assign bit_extender_1_out = {{31{1'b0}}, Cin};  // Bit_Extender bit_extender_1
  Multiplier_part #(.width(32)) multiplier_1 (
    .a(A), .b(B), .out(Result), .cin(bit_extender_1_out), .cout(multiplier_1_cout));
  Comparator #(.width(32)) comparator_1 (.a(multiplier_1_cout), .b({32{1'b0}}), .gt(Carry_Flag));  // open: eq, lt

  // Notes on the sheet:
  //   ALU - B98729
  //   Inputs
  //   Outputs
endmodule

module ALU (
  input  Cin,
  input  [3:0] Opcode,
  input  [31:0] A,
  input  [31:0] B,
  output [31:0] Y,
  output Zero_Flag,
  output Cout
);

  wire adder_1_overflow, comparator_1_lt, multiplier_1_carry_flag, subtractor_1_bout;
  wire [4:0] bitselector_1_out;
  wire [6:0] bitadder_1_out;
  wire [31:0] adder_1_result, and_1_out, bit_extender_1_out, bit_extender_2_out, divider_1_out,
       divider_1_rem, multiplier_1_result, nand_1_out, or_1_out, shifter_1_out, shifter_2_out, shifter_3_out,
       shifter_4_out, subtractor_1_out, xnor_1_out, xor_1_out;

  BitSelector #(.width(32), .group(5)) bitselector_1 (.in(B), .out(bitselector_1_out), .sel(3'b000));
  Adder adder_1 (.Cin(Cin), .A(A), .B(B), .Result(adder_1_result), .Overflow(adder_1_overflow));
  assign and_1_out = A & B;  // AND_Gate and_1, 32 bits wide
  assign or_1_out = A | B;  // OR_Gate or_1, 32 bits wide
  assign xor_1_out = A ^ B;  // XOR_Gate xor_1, 32 bits wide
  Shifter #(.width(32), .shift("lr")) shifter_1 (.in(A), .\dist (bitselector_1_out), .out(shifter_1_out));
  Shifter #(.width(32), .shift("ar")) shifter_2 (.in(A), .\dist (bitselector_1_out), .out(shifter_2_out));
  Shifter #(.width(32)) shifter_3 (.in(A), .\dist (bitselector_1_out), .out(shifter_3_out));
  Shifter #(.width(32)) shifter_4 (.in(A), .\dist (bitselector_1_out), .out(shifter_4_out));
  Comparator #(.width(32)) comparator_1 (.a(A), .b(B), .lt(comparator_1_lt));  // open: gt, eq
  assign bit_extender_1_out = {{31{1'b0}}, comparator_1_lt};  // Bit_Extender bit_extender_1
  Divider #(.width(32)) divider_1 (.a(A), .b(B), .out(divider_1_out), .rem(divider_1_rem));  // open: upper
  Multiplier multiplier_1 (.Cin(Cin), .A(A), .B(B), .Result(multiplier_1_result), .Carry_Flag(multiplier_1_carry_flag));
  Subtractor #(.width(32)) subtractor_1 (.a(A), .b(B), .out(subtractor_1_out), .bin(Cin), .bout(subtractor_1_bout));
  BitAdder #(.width(32)) bitadder_1 (.in0(A), .in1(B), .out(bitadder_1_out));
  assign bit_extender_2_out = {{25{1'b0}}, bitadder_1_out};  // Bit_Extender bit_extender_2
  assign nand_1_out = ~(A & B);  // NAND_Gate nand_1, 32 bits wide
  assign xnor_1_out = ~(A ^ B);  // XNOR_Gate xnor_1, 32 bits wide
  or or_2 (Cout, adder_1_overflow, subtractor_1_bout, multiplier_1_carry_flag);
  Multiplexer #(.select(4), .width(32), .enable("false")) multiplexer_1 (
    .in0(adder_1_result), .in1(and_1_out), .in2(or_1_out), .in3(xor_1_out), .in4(shifter_1_out),
    .in5(shifter_2_out), .in6(shifter_3_out), .in7(shifter_4_out), .in8(bit_extender_1_out),
    .in9(divider_1_out), .in10(divider_1_rem), .in11(multiplier_1_result), .in12(subtractor_1_out),
    .in13(bit_extender_2_out), .in14(nand_1_out), .in15(xnor_1_out), .out(Y), .sel(Opcode));
  Comparator #(.width(32)) comparator_2 (.a(Y), .b({32{1'b0}}), .eq(Zero_Flag));  // open: gt, lt

  // Notes on the sheet:
  //   Entradas:
  //   Hay ciertas operaciones, que debido
  //   suma, multiplicación, resta...
  //   A: Operando de 32 bits
  //   B: Operando de 32 bits
  //   Cin: Bit de acarreo
  //   a su naturaleza requieren de circuitos adicionales, por ejemplo
  //   ALU - B98729
  //   Opcode: Código de operación
  //   Salidas:
  //   Y: Resultado de la operación
  //   Zero: Bandera que determina si el resultado es cero
  //   Cout: Bandera que determina si hubo overflow 
  //   Inputs
  //   Outputs
endmodule

// MUX
module PC_Mux (
  input  Branch,
  input  Jump,
  input  [31:0] PC_4,
  input  [31:0] MEM_PC,
  input  [31:0] JUMP_2,
  output [31:0] PC_MUX
);

  wire [31:0] multiplexer_1_out, multiplexer_2_out;

  Multiplexer #(.width(32), .enable("false")) multiplexer_1 (
    .in0(PC_4), .in1(MEM_PC), .out(multiplexer_1_out), .sel(Branch));
  Multiplexer #(.width(32), .enable("false")) multiplexer_2 (
    .in0({32{1'b0}}), .in1(JUMP_2), .out(multiplexer_2_out), .sel(Jump));
  Multiplexer #(.width(32), .enable("false")) multiplexer_3 (
    .in0(multiplexer_1_out), .in1(multiplexer_2_out), .out(PC_MUX), .sel(Jump));

  // Other names for the same wires on the sheet: JUMP_t[31:0] = JUMP_2

  // Notes on the sheet:
  //   B98729 - PC_MUX
  //   de la Unidad de Control
  //   Este circuito sustituye al Multiplexor conectado al PC
  //   Su función es cambiar el valor del Program Counter, dependiendo del tipo de instrucción
  //   Viene de la unidad de control
  //   Ya sea un Branch o Jump, dado que una instrucción no puede ser de ambos tipos,.se usa como fuente del mux la señal JUMP 
  //   Inputs
  //   Outputs
endmodule

module Data_Memory (
  input  [11:0] Address,
  input  [31:0] DataIn,
  input  MemRead,
  input  MemWrite,
  input  Clock,
  input  [1:0] Access_Type,
  output [31:0] DataOut
);

  wire [3:0] ram_selector_1_sel;
  wire [7:0] ram_1_data, ram_2_data, ram_3_data, ram_4_data;
  wire [31:0] data_input_splitter_1_dataout;

  Data_Input_Splitter data_input_splitter_1 (
    .DataIn(DataIn), .Access_Type(Access_Type), .DataOut(data_input_splitter_1_dataout));
  RAM_Selector ram_selector_1 (.Offset(Address[1:0]), .Sel(ram_selector_1_sel), .Access_Type(Access_Type));
  // Probe on data_input_splitter_1_dataout[23:16]
  RAM #(.addrWidth(10), .bus("separate"), .Select("high")) ram_1 (
    .addr(Address[11:2]), .din(data_input_splitter_1_dataout[7:0]), .data(ram_1_data), .str(MemWrite),
    .sel(ram_selector_1_sel[0]), .clk(Clock), .ld(MemRead));  // open: clr
  RAM #(.addrWidth(10), .bus("separate"), .Select("high")) ram_2 (
    .addr(Address[11:2]), .din(data_input_splitter_1_dataout[15:8]), .data(ram_2_data), .str(MemWrite),
    .sel(ram_selector_1_sel[1]), .clk(Clock), .ld(MemRead));  // open: clr
  RAM #(.addrWidth(10), .bus("separate"), .Select("high")) ram_3 (
    .addr(Address[11:2]), .din(data_input_splitter_1_dataout[23:16]), .data(ram_3_data), .str(MemWrite),
    .sel(ram_selector_1_sel[2]), .clk(Clock), .ld(MemRead));  // open: clr
  RAM #(.addrWidth(10), .bus("separate"), .Select("high")) ram_4 (
    .addr(Address[11:2]), .din(data_input_splitter_1_dataout[31:24]), .data(ram_4_data), .str(MemWrite),
    .sel(ram_selector_1_sel[3]), .clk(Clock), .ld(MemRead));  // open: clr
  Data_Output_Splitter data_output_splitter_1 (
    .Data({ram_4_data, ram_3_data, ram_2_data, ram_1_data}), .Offset(Address[1:0]),
    .Access_Type(Access_Type), .DataOut(DataOut));

  // Notes on the sheet:
  //   B98729 - CPU
  //   Byte 0
  //   Byte 2
  //   Byte 3
  //   00 Byte
  //   01 Half
  //   10 Word
  //   Inputs
  //   Outputs
endmodule

module RAM_Selector (
  input  [1:0] Offset,
  input  [1:0] Access_Type,
  output [3:0] Sel
);

  ROM #(.addrWidth(4), .dataWidth(4), .Select("high")) rom_1 (.addr({Access_Type, Offset}), .data(Sel));

  // Notes on the sheet:
  //   B98729 - CPU
  //   contents of rom_1 (hex, n*v repeats v):
  //   1 1 4 4 3 3 c c 4*f
  //   Inputs
  //   Outputs
endmodule

module Data_Input_Splitter (
  input  [31:0] DataIn,
  input  [1:0] Access_Type,
  output [31:0] DataOut
);

  wire [7:0] bitselector_1_out, bitselector_2_out;

  BitSelector #(.width(32), .group(8)) bitselector_1 (.in(DataIn), .out(bitselector_1_out), .sel(2'b00));
  BitSelector #(.width(32), .group(8)) bitselector_2 (.in(DataIn), .out(bitselector_2_out), .sel(2'b01));
  Multiplexer #(.select(2), .width(32), .enable("false")) multiplexer_1 (
    .in0({bitselector_1_out, bitselector_1_out, bitselector_1_out, bitselector_1_out}),
    .in1({bitselector_2_out, bitselector_1_out, bitselector_2_out, bitselector_1_out}), .in2(DataIn),
    .in3({32{1'b0}}), .out(DataOut), .sel(Access_Type));

  // Notes on the sheet:
  //   B98729 - CPU
  //   01 Half
  //   00 Byte
  //   10 Word
  //   Inputs
  //   Outputs
endmodule

module Data_Output_Splitter (
  input  [31:0] Data,
  input  [1:0] Offset,
  input  [1:0] Access_Type,
  output [31:0] DataOut
);

  wire [31:0] bit_extender_1_out, bit_extender_2_out, bit_extender_3_out, bit_extender_4_out,
       multiplexer_1_out, multiplexer_2_out;

  assign bit_extender_1_out = {{24{1'b0}}, Data[7:0]};  // Bit_Extender bit_extender_1
  assign bit_extender_2_out = {{24{1'b0}}, Data[23:16]};  // Bit_Extender bit_extender_2
  assign bit_extender_3_out = {{16{1'b0}}, Data[15:0]};  // Bit_Extender bit_extender_3
  assign bit_extender_4_out = {{16{1'b0}}, Data[31:16]};  // Bit_Extender bit_extender_4
  Multiplexer #(.select(2), .width(32), .enable("false")) multiplexer_1 (
    .in0(bit_extender_1_out), .in1(bit_extender_1_out), .in2(bit_extender_2_out), .in3(bit_extender_2_out),
    .out(multiplexer_1_out), .sel(Offset));
  Multiplexer #(.select(2), .width(32), .enable("false")) multiplexer_2 (
    .in0(bit_extender_3_out), .in1(bit_extender_3_out), .in2(bit_extender_4_out), .in3(bit_extender_4_out),
    .out(multiplexer_2_out), .sel(Offset));
  Multiplexer #(.select(2), .width(32), .enable("false")) multiplexer_3 (
    .in0(multiplexer_1_out), .in1(multiplexer_2_out), .in2(Data), .out(DataOut), .sel(Access_Type));  // open: in3

  // Notes on the sheet:
  //   B98729 - CPU
  //   LH
  //   00 Byte
  //   01 Half
  //   10 Word
  //   Inputs
  //   Outputs
endmodule
